// Logisim project project.circ as structural Verilog
module main (
  input  _0,
  input  Load,
  input  _1,
  input  _2,
  input  _3,
  input  _4,
  input  _5,
  input  _6,
  input  _7,
  input  _8,
  input  _9
);

  wire addif5_1_out_6, addif5_1_out_7, addif5_1_out_8, addif5_1_out_9, addif5_2_out_6, addif5_2_out_7,
       addif5_2_out_8, addif5_2_out_9, addif5_3_out_6, addif5_3_out_7, addif5_3_out_8, addif5_3_out_9,
       addif5_4_out_6, addif5_4_out_7, addif5_4_out_8, addif5_4_out_9, addif5_5_out_6, addif5_5_out_7,
       addif5_5_out_8, addif5_5_out_9, addif5_6_out_6, addif5_6_out_7, addif5_6_out_8, addif5_6_out_9,
       addif5_7_out_6, addif5_7_out_7, addif5_7_out_8, addif5_7_out_9, and_1_out, and_2_out, and_3_out,
       and_4_out, BEQ_out_3, control_unit_1_inc, control_unit_1_jump, control_unit_1_mode,
       control_unit_1_out_12, control_unit_1_out_13, control_unit_1_pc__mar, control_unit_1_print,
       control_unit_1_stop, control_unit_1_sys__mbr, control_unit_1_tick_0, control_unit_1_tick_1,
       control_unit_1_tick_2, CPU_CLOCK_out, n2bitdisplay_1_s1, n2bitdisplay_1_s2, n2bitdisplay_1_s3,
       n2bitdisplay_1_s4, n2bitdisplay_1_s5, n2bitdisplay_1_s6, n2bitdisplay_1_s7, n2bitdisplay_1_s8,
       n4bitdisplay_1_out_5, n4bitdisplay_1_out_6, n4bitdisplay_1_out_7, n4bitdisplay_1_out_8,
       n4bitdisplay_1_out_9, n4bitdisplay_1_out_10, n4bitdisplay_1_out_11, n4bitdisplay_1_out_12,
       n4bitdisplay_2_out_5, n4bitdisplay_2_out_6, n4bitdisplay_2_out_7, n4bitdisplay_2_out_8,
       n4bitdisplay_2_out_9, n4bitdisplay_2_out_10, n4bitdisplay_2_out_11, n4bitdisplay_2_out_12, not_1_out,
       not_2_out, or_1_out, t_ff_1_q;
  wire [1:0] control_unit_1_out_9, control_unit_1_select_read_from_cpu_bus,
       control_unit_1_select_write_to_cpu_bus;
  wire [2:0] alu_1_zero_output, Status_out_2;
  wire [3:0] AR_out_2, INC_sum, IR_out_3, multiplexer_1_out, multiplexer_2_out, n4bit_register_1_out_3,
       PC_out_3;
  wire [7:0] alu_1_out_13, demultiplexer_1_out0, demultiplexer_1_out1, demultiplexer_1_out3,
       demultiplexer_2_out0, demultiplexer_2_out1, demultiplexer_3_out0, demultiplexer_3_out1,
       demultiplexer_3_out2, demultiplexer_3_out3, demultiplexer_3_out4, demultiplexer_3_out5,
       demultiplexer_3_out6, demultiplexer_3_out7, demultiplexer_3_out8, demultiplexer_3_out9,
       demultiplexer_3_out10, demultiplexer_3_out11, demultiplexer_3_out12, demultiplexer_3_out13,
       demultiplexer_3_out14, demultiplexer_3_out15, DR_out_2, inputbuffer_1_out_11, MBR_out_3,
       multiplexer_3_out, multiplexer_4_out, multiplexer_5_out, multiplexer_6_out, multiplexer_7_out,
       multiplexer_8_out, n2_s_complement_1_out_4, n8bit_register_1_out_3, n8bit_register_2_out_3,
       n8bit_register_3_out_3, n8bit_register_4_out_3, n8bit_register_5_out_3, n8bit_register_6_out_3,
       n8bit_register_7_out_3, n8bit_register_8_out_3, n8bit_register_9_out_3, n8bit_register_10_out_3,
       n8bit_register_11_out_3, n8bit_register_12_out_3, n8bit_register_13_out_3, n8bit_register_14_out_3,
       n8bit_register_15_out_3, n8bit_register_16_out_3, n8bit_register_17_out_3, n8bit_register_18_out_3,
       n8bit_rising_reg_1_out_3, n8bit_rising_reg_2_out_3, R1_out_3, R2_out_3, romwrite_1_out_34,
       romwrite_1_out_35, romwrite_1_out_36, romwrite_1_out_37, romwrite_1_out_38, romwrite_1_out_39,
       romwrite_1_out_40, romwrite_1_out_41, romwrite_1_out_42, romwrite_1_out_43, romwrite_1_out_44,
       romwrite_1_out_45, romwrite_1_out_46, romwrite_1_out_47, romwrite_1_out_48, romwrite_1_out_49;
  wire [7:4] IR_out_3_2;

  not not_1 (not_1_out, t_ff_1_q);
  ALU alu_1 (
    .in_1(control_unit_1_out_12), .in_2(control_unit_1_out_13), .zero_output(alu_1_zero_output[0]),
    .out_6(alu_1_out_13[7]), .out_7(alu_1_out_13[6]), .out_8(alu_1_out_13[5]), .out_9(alu_1_out_13[4]),
    .out_10(alu_1_out_13[3]), .out_11(alu_1_out_13[2]), .out_12(alu_1_out_13[1]), .out_13(alu_1_out_13[0]),
    .overflow_output(alu_1_zero_output[1]), .in_4(n8bit_register_1_out_3), .in_3(n8bit_register_2_out_3),
    .neg_output(alu_1_zero_output[2]));
  Clock CPU_CLOCK (.out(CPU_CLOCK_out));
  and and_1 (and_1_out, CPU_CLOCK_out, not_1_out, control_unit_1_tick_0);
  Multiplexer #(.width(4), .disabled(0), .enable("false")) multiplexer_1 (
    .in0(INC_sum), .in1(IR_out_3), .out(multiplexer_1_out), .sel(control_unit_1_jump));
  and and_2 (and_2_out, not_1_out, control_unit_1_stop);
  control_unit control_unit_1 (
    .in_3({IR_out_3_2, IR_out_3}), .Mode(control_unit_1_mode), .sys__mbr(control_unit_1_sys__mbr),
    .select_write_to_cpu_bus(control_unit_1_select_write_to_cpu_bus),
    .select_read_from_cpu_bus(control_unit_1_select_read_from_cpu_bus), .out_9(control_unit_1_out_9),
    .tick_0(control_unit_1_tick_0), .clock(CPU_CLOCK_out), .pc__mar(control_unit_1_pc__mar),
    .tick_1(control_unit_1_tick_1), .print(control_unit_1_print), .out_12(control_unit_1_out_12),
    .out_13(control_unit_1_out_13), .Jump(control_unit_1_jump), .Branch_Test(BEQ_out_3),
    .stop(control_unit_1_stop), .tick_2(control_unit_1_tick_2), .inc(control_unit_1_inc));
  _2_s_Complement u_2_s_complement_1 (
    .in_1(control_unit_1_out_12), .in_2(control_unit_1_out_13), .in_3(R1_out_3),
    .out_4(n2_s_complement_1_out_4));
  _8bit_Register u_8bit_register_1 (
    .clock_input(control_unit_1_tick_1), .in_2(n2_s_complement_1_out_4), .out_3(n8bit_register_1_out_3));
  _4bit_rising_reg PC (.CU_input(and_1_out), .in_2(multiplexer_1_out), .out_3(PC_out_3));
  // Probe on PC_out_3
  T_Flip_Flop t_ff_1 (.clk(CPU_CLOCK_out), .T(and_2_out), .Q(t_ff_1_q));  // open: Qn, preset, reset, en
  _4_bit_adder INC (.in_1(4'b0001), .in_2(PC_out_3), .Sum(INC_sum));  // open: Overflow
  _4bit_Register u_4bit_register_1 (.CU_input(CPU_CLOCK_out), .in_2(multiplexer_2_out), .out_3(n4bit_register_1_out_3));
  // Probe on n4bit_register_1_out_3
  Multiplexer #(.width(4), .disabled(0), .enable("false")) multiplexer_2 (
    .in0(IR_out_3), .in1(PC_out_3), .out(multiplexer_2_out), .sel(control_unit_1_pc__mar));
  _8bit_Register R1 (.clock_input(control_unit_1_tick_2), .in_2(demultiplexer_1_out1), .out_3(R1_out_3));
  Multiplexer #(.width(8), .disabled(0), .enable("false")) multiplexer_3 (
    .in0(R2_out_3), .in1(8'h1), .out(multiplexer_3_out), .sel(control_unit_1_inc));
  and and_3 (and_3_out, not_2_out, control_unit_1_tick_0);
  not not_2 (not_2_out, t_ff_1_q);
  A_B_comparator_2 BEQ (.in_2(R1_out_3), .out_3(BEQ_out_3), .in_1(R2_out_3));
  _8bit_Register R2 (.clock_input(control_unit_1_tick_2), .in_2(demultiplexer_1_out3), .out_3(R2_out_3));
  Multiplexer #(.select(2), .width(8)) multiplexer_4 (
    .in0(MBR_out_3), .in1(R1_out_3), .in2(n8bit_rising_reg_1_out_3), .in3(R2_out_3), .out(multiplexer_4_out),
    .sel(control_unit_1_select_write_to_cpu_bus), .en(CPU_CLOCK_out));
  Demultiplexer #(.select(2), .width(8), .tristate("true"), .enable("false")) demultiplexer_1 (
    .out0(demultiplexer_1_out0), .out1(demultiplexer_1_out1), .out3(demultiplexer_1_out3),
    .in(multiplexer_4_out), .sel(control_unit_1_select_read_from_cpu_bus));  // open: out2
  _8bit_Register u_8bit_register_2 (
    .clock_input(control_unit_1_tick_1), .in_2(multiplexer_3_out), .out_3(n8bit_register_2_out_3));
  _8bit_rising_reg u_8bit_rising_reg_1 (
    .clock_input(CPU_CLOCK_out), .in_2(alu_1_out_13), .out_3(n8bit_rising_reg_1_out_3));
  Multiplexer #(.width(8), .disabled(0), .enable("false")) multiplexer_5 (
    .in0(demultiplexer_1_out0), .in1(multiplexer_6_out), .out(multiplexer_5_out),
    .sel(control_unit_1_sys__mbr));
  // Probe on {IR_out_3_2, IR_out_3}
  _8bit_Register IR (.clock_input(and_3_out), .in_2(MBR_out_3), .out_3({IR_out_3_2, IR_out_3}));
  // Probe on Status_out_2
  _3bit_async_reg Status (.in_1(alu_1_zero_output), .out_2(Status_out_2));
  _8bit_Register MBR (.clock_input(CPU_CLOCK_out), .in_2(multiplexer_5_out), .out_3(MBR_out_3));
  _2bitdisplay u_2bitdisplay_1 (
    .a(addif5_2_out_9), .b(addif5_3_out_9), .s1(n2bitdisplay_1_s1), .s2(n2bitdisplay_1_s2),
    .s3(n2bitdisplay_1_s3), .s4(n2bitdisplay_1_s4), .s5(n2bitdisplay_1_s5), .s6(n2bitdisplay_1_s6),
    .s7(n2bitdisplay_1_s7), .s8(n2bitdisplay_1_s8));
  _7_Segment_Display u_7_segment_display_1 (
    .g(n2bitdisplay_1_s1), .f(n2bitdisplay_1_s2), .a(n2bitdisplay_1_s3), .b(n2bitdisplay_1_s4),
    .e(n2bitdisplay_1_s5), .d(n2bitdisplay_1_s6), .c(n2bitdisplay_1_s7), .dp(n2bitdisplay_1_s8));
  Multiplexer #(.select(2), .width(8), .disabled(0), .enable("false")) multiplexer_6 (
    .in0(demultiplexer_2_out0), .in1(MBR_out_3), .in2(inputbuffer_1_out_11), .out(multiplexer_6_out),
    .sel(control_unit_1_out_9));  // open: in3
  _4bitdisplay u_4bitdisplay_1 (
    .a(addif5_3_out_8), .b(addif5_3_out_7), .c(addif5_3_out_6), .d(addif5_7_out_9),
    .out_9(n4bitdisplay_1_out_9), .out_10(n4bitdisplay_1_out_10), .out_11(n4bitdisplay_1_out_11),
    .out_12(n4bitdisplay_1_out_12), .out_5(n4bitdisplay_1_out_5), .out_6(n4bitdisplay_1_out_6),
    .out_7(n4bitdisplay_1_out_7), .out_8(n4bitdisplay_1_out_8));
  _7_Segment_Display u_7_segment_display_2 (
    .g(n4bitdisplay_1_out_5), .f(n4bitdisplay_1_out_6), .a(n4bitdisplay_1_out_7), .b(n4bitdisplay_1_out_8),
    .e(n4bitdisplay_1_out_9), .d(n4bitdisplay_1_out_10), .c(n4bitdisplay_1_out_11), .dp(n4bitdisplay_1_out_12));
  _4bitdisplay u_4bitdisplay_2 (
    .a(addif5_7_out_8), .b(addif5_7_out_7), .c(addif5_7_out_6), .d(n8bit_rising_reg_2_out_3[0]),
    .out_9(n4bitdisplay_2_out_9), .out_10(n4bitdisplay_2_out_10), .out_11(n4bitdisplay_2_out_11),
    .out_12(n4bitdisplay_2_out_12), .out_5(n4bitdisplay_2_out_5), .out_6(n4bitdisplay_2_out_6),
    .out_7(n4bitdisplay_2_out_7), .out_8(n4bitdisplay_2_out_8));
  _8_bit_async_reg DR (.in_1(multiplexer_7_out), .out_2(DR_out_2));
  Multiplexer #(.width(8), .disabled(0), .enable("false")) multiplexer_7 (
    .in0(multiplexer_8_out), .in1(multiplexer_6_out), .out(multiplexer_7_out), .sel(control_unit_1_mode));
  _4_bit_async_reg AR (.in_1(n4bit_register_1_out_3), .out_2(AR_out_2));
  // Probe on inputbuffer_1_out_11
  inputbuffer inputbuffer_1 (
    ._0(_0), ._1(_1), ._2(_2), ._3(_3), ._4(_4), ._5(_5), ._6(_6), ._7(_7), ._8(_8), ._9(_9),
    .out_11(inputbuffer_1_out_11));
  _7_Segment_Display u_7_segment_display_3 (
    .g(n4bitdisplay_2_out_5), .f(n4bitdisplay_2_out_6), .a(n4bitdisplay_2_out_7), .b(n4bitdisplay_2_out_8),
    .e(n4bitdisplay_2_out_9), .d(n4bitdisplay_2_out_10), .c(n4bitdisplay_2_out_11), .dp(n4bitdisplay_2_out_12));
  Demultiplexer #(.width(8), .enable("false")) demultiplexer_2 (
    .out0(demultiplexer_2_out0), .out1(demultiplexer_2_out1), .in(DR_out_2), .sel(control_unit_1_mode));
  Demultiplexer #(.select(4), .width(8), .tristate("true")) demultiplexer_3 (
    .out0(demultiplexer_3_out0), .out1(demultiplexer_3_out1), .out2(demultiplexer_3_out2),
    .out3(demultiplexer_3_out3), .out4(demultiplexer_3_out4), .out5(demultiplexer_3_out5),
    .out6(demultiplexer_3_out6), .out7(demultiplexer_3_out7), .out8(demultiplexer_3_out8),
    .out9(demultiplexer_3_out9), .out10(demultiplexer_3_out10), .out11(demultiplexer_3_out11),
    .out12(demultiplexer_3_out12), .out13(demultiplexer_3_out13), .out14(demultiplexer_3_out14),
    .out15(demultiplexer_3_out15), .in(demultiplexer_2_out1), .sel(AR_out_2), .en(and_4_out));
  addif5 addif5_1 (
    .in_1(n8bit_rising_reg_2_out_3[5]), .in_2(n8bit_rising_reg_2_out_3[6]),
    .in_3(n8bit_rising_reg_2_out_3[7]), .in_4(1'b0), .out_6(addif5_1_out_6), .out_7(addif5_1_out_7),
    .out_8(addif5_1_out_8), .out_9(addif5_1_out_9));  // open: Overflow
  addif5 addif5_2 (
    .in_1(addif5_5_out_9), .in_2(addif5_4_out_9), .in_3(addif5_1_out_9), .in_4(1'b0), .out_6(addif5_2_out_6),
    .out_7(addif5_2_out_7), .out_8(addif5_2_out_8), .out_9(addif5_2_out_9));  // open: Overflow
  addif5 addif5_3 (
    .in_1(addif5_6_out_9), .in_2(addif5_2_out_6), .in_3(addif5_2_out_7), .in_4(addif5_2_out_8),
    .out_6(addif5_3_out_6), .out_7(addif5_3_out_7), .out_8(addif5_3_out_8), .out_9(addif5_3_out_9));  // open: Overflow
  _8bit_rising_reg u_8bit_rising_reg_2 (
    .clock_input(control_unit_1_print), .in_2(multiplexer_6_out), .out_3(n8bit_rising_reg_2_out_3));
  addif5 addif5_4 (
    .in_1(n8bit_rising_reg_2_out_3[4]), .in_2(addif5_1_out_6), .in_3(addif5_1_out_7), .in_4(addif5_1_out_8),
    .out_6(addif5_4_out_6), .out_7(addif5_4_out_7), .out_8(addif5_4_out_8), .out_9(addif5_4_out_9));  // open: Overflow
  addif5 addif5_5 (
    .in_1(n8bit_rising_reg_2_out_3[3]), .in_2(addif5_4_out_6), .in_3(addif5_4_out_7), .in_4(addif5_4_out_8),
    .out_6(addif5_5_out_6), .out_7(addif5_5_out_7), .out_8(addif5_5_out_8), .out_9(addif5_5_out_9));  // open: Overflow
  addif5 addif5_6 (
    .in_1(n8bit_rising_reg_2_out_3[2]), .in_2(addif5_5_out_6), .in_3(addif5_5_out_7), .in_4(addif5_5_out_8),
    .out_6(addif5_6_out_6), .out_7(addif5_6_out_7), .out_8(addif5_6_out_8), .out_9(addif5_6_out_9));  // open: Overflow
  addif5 addif5_7 (
    .in_1(n8bit_rising_reg_2_out_3[1]), .in_2(addif5_6_out_6), .in_3(addif5_6_out_7), .in_4(addif5_6_out_8),
    .out_6(addif5_7_out_6), .out_7(addif5_7_out_7), .out_8(addif5_7_out_8), .out_9(addif5_7_out_9));  // open: Overflow
  and and_4 (and_4_out, control_unit_1_mode, CPU_CLOCK_out);
  _8bit_Register u_8bit_register_3 (.clock_input(or_1_out), .in_2(romwrite_1_out_34), .out_3(n8bit_register_3_out_3));
  _8bit_Register u_8bit_register_4 (.clock_input(or_1_out), .in_2(romwrite_1_out_35), .out_3(n8bit_register_4_out_3));
  _8bit_Register u_8bit_register_5 (.clock_input(or_1_out), .in_2(romwrite_1_out_36), .out_3(n8bit_register_5_out_3));
  _8bit_Register u_8bit_register_6 (.clock_input(or_1_out), .in_2(romwrite_1_out_37), .out_3(n8bit_register_6_out_3));
  _8bit_Register u_8bit_register_7 (.clock_input(or_1_out), .in_2(romwrite_1_out_38), .out_3(n8bit_register_7_out_3));
  _8bit_Register u_8bit_register_8 (.clock_input(or_1_out), .in_2(romwrite_1_out_39), .out_3(n8bit_register_8_out_3));
  _8bit_Register u_8bit_register_9 (.clock_input(or_1_out), .in_2(romwrite_1_out_40), .out_3(n8bit_register_9_out_3));
  _8bit_Register u_8bit_register_10 (.clock_input(or_1_out), .in_2(romwrite_1_out_41), .out_3(n8bit_register_10_out_3));
  _8bit_Register u_8bit_register_11 (.clock_input(or_1_out), .in_2(romwrite_1_out_42), .out_3(n8bit_register_11_out_3));
  _8bit_Register u_8bit_register_12 (.clock_input(or_1_out), .in_2(romwrite_1_out_43), .out_3(n8bit_register_12_out_3));
  _8bit_Register u_8bit_register_13 (.clock_input(or_1_out), .in_2(romwrite_1_out_44), .out_3(n8bit_register_13_out_3));
  _8bit_Register u_8bit_register_14 (.clock_input(or_1_out), .in_2(romwrite_1_out_45), .out_3(n8bit_register_14_out_3));
  _8bit_Register u_8bit_register_15 (.clock_input(or_1_out), .in_2(romwrite_1_out_46), .out_3(n8bit_register_15_out_3));
  _8bit_Register u_8bit_register_16 (.clock_input(or_1_out), .in_2(romwrite_1_out_47), .out_3(n8bit_register_16_out_3));
  _8bit_Register u_8bit_register_17 (.clock_input(or_1_out), .in_2(romwrite_1_out_48), .out_3(n8bit_register_17_out_3));
  _8bit_Register u_8bit_register_18 (.clock_input(or_1_out), .in_2(romwrite_1_out_49), .out_3(n8bit_register_18_out_3));
  RomWrite romwrite_1 (
    .in_1(demultiplexer_3_out0), .in_3(demultiplexer_3_out1), .in_5(demultiplexer_3_out2),
    .in_7(demultiplexer_3_out3), .in_9(demultiplexer_3_out4), .in_11(demultiplexer_3_out5),
    .in_13(demultiplexer_3_out6), .in_15(demultiplexer_3_out7), .in_17(demultiplexer_3_out8),
    .in_19(demultiplexer_3_out9), .in_21(demultiplexer_3_out10), .in_23(demultiplexer_3_out11),
    .in_25(demultiplexer_3_out12), .in_27(demultiplexer_3_out13), .in_29(demultiplexer_3_out14),
    .in_31(demultiplexer_3_out15), .in_2(8'hd), .in_4(8'hd8), .in_6(8'h8a), .in_8(8'h44), .in_10(8'h2d),
    .in_12(8'hf), .in_14(8'h1e), .in_16(8'h40), .in_18(8'h2e), .in_20(8'hf0), .in_22(8'he), .in_24(8'hc0),
    .in_26(8'he0), .in_28({8{1'b0}}), .in_30({8{1'b0}}), .in_32({8{1'b1}}), .in_33(Load),
    .out_34(romwrite_1_out_34), .out_35(romwrite_1_out_35), .out_36(romwrite_1_out_36),
    .out_37(romwrite_1_out_37), .out_38(romwrite_1_out_38), .out_39(romwrite_1_out_39),
    .out_40(romwrite_1_out_40), .out_41(romwrite_1_out_41), .out_42(romwrite_1_out_42),
    .out_43(romwrite_1_out_43), .out_44(romwrite_1_out_44), .out_45(romwrite_1_out_45),
    .out_46(romwrite_1_out_46), .out_47(romwrite_1_out_47), .out_48(romwrite_1_out_48),
    .out_49(romwrite_1_out_49));
  Multiplexer #(.select(4), .width(8), .disabled(0), .enable("false")) multiplexer_8 (
    .in0(n8bit_register_3_out_3), .in1(n8bit_register_4_out_3), .in2(n8bit_register_5_out_3),
    .in3(n8bit_register_6_out_3), .in4(n8bit_register_7_out_3), .in5(n8bit_register_8_out_3),
    .in6(n8bit_register_9_out_3), .in7(n8bit_register_10_out_3), .in8(n8bit_register_11_out_3),
    .in9(n8bit_register_12_out_3), .in10(n8bit_register_13_out_3), .in11(n8bit_register_14_out_3),
    .in12(n8bit_register_15_out_3), .in13(n8bit_register_16_out_3), .in14(n8bit_register_17_out_3),
    .in15(n8bit_register_18_out_3), .out(multiplexer_8_out), .sel(AR_out_2));
  or or_1 (or_1_out, and_4_out, Load);

  // Notes on the sheet:
  //   Data bus
  //   Address Bus
  //   Data Bus
  //   Address bus
  //   MR
endmodule

module _8bit_Register (
  input  clock_input,
  input  [7:0] in_2,
  output [7:0] out_3
);

  D_Flip_Flop #(.trigger("high")) d_ff_1 (.clk(clock_input), .D(in_2[7]), .Q(out_3[7]));  // open: Qn, preset, en, reset
  D_Flip_Flop #(.trigger("high")) d_ff_2 (.clk(clock_input), .D(in_2[6]), .Q(out_3[6]));  // open: Qn, preset, en, reset
  D_Flip_Flop #(.trigger("high")) d_ff_3 (.clk(clock_input), .D(in_2[5]), .Q(out_3[5]));  // open: Qn, preset, en, reset
  D_Flip_Flop #(.trigger("high")) d_ff_4 (.clk(clock_input), .D(in_2[4]), .Q(out_3[4]));  // open: Qn, preset, en, reset
  D_Flip_Flop #(.trigger("high")) d_ff_5 (.clk(clock_input), .D(in_2[3]), .Q(out_3[3]));  // open: Qn, preset, en, reset
  D_Flip_Flop #(.trigger("high")) d_ff_6 (.clk(clock_input), .D(in_2[2]), .Q(out_3[2]));  // open: Qn, preset, en, reset
  D_Flip_Flop #(.trigger("high")) d_ff_7 (.clk(clock_input), .D(in_2[1]), .Q(out_3[1]));  // open: Qn, preset, en, reset
  D_Flip_Flop #(.trigger("high")) d_ff_8 (.clk(clock_input), .D(in_2[0]), .Q(out_3[0]));  // open: Qn, preset, en, reset
endmodule

module _4bit_Register (
  input  CU_input,
  input  [3:0] in_2,
  output [3:0] out_3
);

  D_Flip_Flop #(.trigger("high")) d_ff_1 (.clk(CU_input), .D(in_2[2]), .Q(out_3[2]));  // open: Qn, preset, en, reset
  D_Flip_Flop #(.trigger("high")) d_ff_2 (.clk(CU_input), .D(in_2[3]), .Q(out_3[3]));  // open: Qn, preset, en, reset
  D_Flip_Flop #(.trigger("high")) d_ff_3 (.clk(CU_input), .D(in_2[1]), .Q(out_3[1]));  // open: Qn, preset, en, reset
  D_Flip_Flop #(.trigger("high")) d_ff_4 (.clk(CU_input), .D(in_2[0]), .Q(out_3[0]));  // open: Qn, preset, en, reset
endmodule

module half_adder (
  input  in_1,
  input  in_2,
  output sum_out,
  output carry_out
);

  xor xor_1 (sum_out, in_1, in_2);
  and and_1 (carry_out, in_1, in_2);
endmodule

module full_adder (
  input  in_1,
  input  in_2,
  input  carry,
  output carry_out,
  output sum_out
);

  wire half_adder_2_carry_out, half_adder_carry_out, half_adder_sum_out;

  half_adder half_adder (.in_1(in_1), .in_2(in_2), .sum_out(half_adder_sum_out), .carry_out(half_adder_carry_out));
  half_adder half_adder_2 (
    .in_1(half_adder_sum_out), .in_2(carry), .sum_out(sum_out), .carry_out(half_adder_2_carry_out));
  or or_1 (carry_out, half_adder_carry_out, half_adder_2_carry_out);
endmodule

module _4_bit_adder (
  input  [3:0] in_1,
  input  [3:0] in_2,
  output Overflow,
  output [3:0] Sum
);

  wire full_adder_1_carry_out, full_adder_3_carry_out, half_adder_1_carry_out;

  half_adder half_adder_1 (.in_1(in_1[0]), .in_2(in_2[0]), .sum_out(Sum[0]), .carry_out(half_adder_1_carry_out));
  full_adder full_adder_1 (
    .in_1(in_1[1]), .in_2(in_2[1]), .carry(half_adder_1_carry_out), .carry_out(full_adder_1_carry_out),
    .sum_out(Sum[1]));
  full_adder full_adder_2 (
    .in_1(in_1[3]), .in_2(in_2[3]), .carry(full_adder_3_carry_out), .carry_out(Overflow), .sum_out(Sum[3]));
  full_adder full_adder_3 (
    .in_1(in_1[2]), .in_2(in_2[2]), .carry(full_adder_1_carry_out), .carry_out(full_adder_3_carry_out),
    .sum_out(Sum[2]));
endmodule

module display (
  input  [7:0] in_1
);

  wire addif5_1_out_6, addif5_1_out_7, addif5_1_out_8, addif5_1_out_9, addif5_2_out_6, addif5_2_out_7,
       addif5_2_out_8, addif5_2_out_9, addif5_3_out_6, addif5_3_out_7, addif5_3_out_8, addif5_3_out_9,
       addif5_4_out_6, addif5_4_out_7, addif5_4_out_8, addif5_4_out_9, addif5_5_out_6, addif5_5_out_7,
       addif5_5_out_8, addif5_5_out_9, addif5_6_out_6, addif5_6_out_7, addif5_6_out_8, addif5_6_out_9,
       addif5_7_out_6, addif5_7_out_7, addif5_7_out_8, addif5_7_out_9, n2bitdisplay_1_s1, n2bitdisplay_1_s2,
       n2bitdisplay_1_s3, n2bitdisplay_1_s4, n2bitdisplay_1_s5, n2bitdisplay_1_s6, n2bitdisplay_1_s7,
       n2bitdisplay_1_s8, n4bitdisplay_1_out_5, n4bitdisplay_1_out_6, n4bitdisplay_1_out_7,
       n4bitdisplay_1_out_8, n4bitdisplay_1_out_9, n4bitdisplay_1_out_10, n4bitdisplay_1_out_11,
       n4bitdisplay_1_out_12, n4bitdisplay_2_out_5, n4bitdisplay_2_out_6, n4bitdisplay_2_out_7,
       n4bitdisplay_2_out_8, n4bitdisplay_2_out_9, n4bitdisplay_2_out_10, n4bitdisplay_2_out_11,
       n4bitdisplay_2_out_12;

  _2bitdisplay u_2bitdisplay_1 (
    .a(addif5_1_out_9), .b(addif5_2_out_9), .s1(n2bitdisplay_1_s1), .s2(n2bitdisplay_1_s2),
    .s3(n2bitdisplay_1_s3), .s4(n2bitdisplay_1_s4), .s5(n2bitdisplay_1_s5), .s6(n2bitdisplay_1_s6),
    .s7(n2bitdisplay_1_s7), .s8(n2bitdisplay_1_s8));
  _7_Segment_Display u_7_segment_display_1 (
    .g(n2bitdisplay_1_s1), .f(n2bitdisplay_1_s2), .a(n2bitdisplay_1_s3), .b(n2bitdisplay_1_s4),
    .e(n2bitdisplay_1_s5), .d(n2bitdisplay_1_s6), .c(n2bitdisplay_1_s7), .dp(n2bitdisplay_1_s8));
  addif5 addif5_1 (
    .in_1(addif5_5_out_9), .in_2(addif5_4_out_9), .in_3(addif5_3_out_9), .in_4(1'b0), .out_6(addif5_1_out_6),
    .out_7(addif5_1_out_7), .out_8(addif5_1_out_8), .out_9(addif5_1_out_9));  // open: Overflow
  addif5 addif5_2 (
    .in_1(addif5_6_out_9), .in_2(addif5_1_out_6), .in_3(addif5_1_out_7), .in_4(addif5_1_out_8),
    .out_6(addif5_2_out_6), .out_7(addif5_2_out_7), .out_8(addif5_2_out_8), .out_9(addif5_2_out_9));  // open: Overflow
  addif5 addif5_3 (
    .in_1(in_1[5]), .in_2(in_1[6]), .in_3(in_1[7]), .in_4(1'b0), .out_6(addif5_3_out_6),
    .out_7(addif5_3_out_7), .out_8(addif5_3_out_8), .out_9(addif5_3_out_9));  // open: Overflow
  addif5 addif5_4 (
    .in_1(in_1[4]), .in_2(addif5_3_out_6), .in_3(addif5_3_out_7), .in_4(addif5_3_out_8),
    .out_6(addif5_4_out_6), .out_7(addif5_4_out_7), .out_8(addif5_4_out_8), .out_9(addif5_4_out_9));  // open: Overflow
  addif5 addif5_5 (
    .in_1(in_1[3]), .in_2(addif5_4_out_6), .in_3(addif5_4_out_7), .in_4(addif5_4_out_8),
    .out_6(addif5_5_out_6), .out_7(addif5_5_out_7), .out_8(addif5_5_out_8), .out_9(addif5_5_out_9));  // open: Overflow
  addif5 addif5_6 (
    .in_1(in_1[2]), .in_2(addif5_5_out_6), .in_3(addif5_5_out_7), .in_4(addif5_5_out_8),
    .out_6(addif5_6_out_6), .out_7(addif5_6_out_7), .out_8(addif5_6_out_8), .out_9(addif5_6_out_9));  // open: Overflow
  addif5 addif5_7 (
    .in_1(in_1[1]), .in_2(addif5_6_out_6), .in_3(addif5_6_out_7), .in_4(addif5_6_out_8),
    .out_6(addif5_7_out_6), .out_7(addif5_7_out_7), .out_8(addif5_7_out_8), .out_9(addif5_7_out_9));  // open: Overflow
  _7_Segment_Display u_7_segment_display_2 (
    .g(n4bitdisplay_1_out_5), .f(n4bitdisplay_1_out_6), .a(n4bitdisplay_1_out_7), .b(n4bitdisplay_1_out_8),
    .e(n4bitdisplay_1_out_9), .d(n4bitdisplay_1_out_10), .c(n4bitdisplay_1_out_11), .dp(n4bitdisplay_1_out_12));
  _4bitdisplay u_4bitdisplay_1 (
    .a(addif5_2_out_8), .b(addif5_2_out_7), .c(addif5_2_out_6), .d(addif5_7_out_9),
    .out_9(n4bitdisplay_1_out_9), .out_10(n4bitdisplay_1_out_10), .out_11(n4bitdisplay_1_out_11),
    .out_12(n4bitdisplay_1_out_12), .out_5(n4bitdisplay_1_out_5), .out_6(n4bitdisplay_1_out_6),
    .out_7(n4bitdisplay_1_out_7), .out_8(n4bitdisplay_1_out_8));
  _4bitdisplay u_4bitdisplay_2 (
    .a(addif5_7_out_8), .b(addif5_7_out_7), .c(addif5_7_out_6), .d(in_1[0]), .out_9(n4bitdisplay_2_out_9),
    .out_10(n4bitdisplay_2_out_10), .out_11(n4bitdisplay_2_out_11), .out_12(n4bitdisplay_2_out_12),
    .out_5(n4bitdisplay_2_out_5), .out_6(n4bitdisplay_2_out_6), .out_7(n4bitdisplay_2_out_7),
    .out_8(n4bitdisplay_2_out_8));
  _7_Segment_Display u_7_segment_display_3 (
    .g(n4bitdisplay_2_out_5), .f(n4bitdisplay_2_out_6), .a(n4bitdisplay_2_out_7), .b(n4bitdisplay_2_out_8),
    .e(n4bitdisplay_2_out_9), .d(n4bitdisplay_2_out_10), .c(n4bitdisplay_2_out_11), .dp(n4bitdisplay_2_out_12));

  // Notes on the sheet:
  //   hunds
  //   tens
  //   ones
endmodule

module addif5 (
  input  in_1,
  input  in_2,
  input  in_3,
  input  in_4,
  output Overflow,
  output out_6,
  output out_7,
  output out_8,
  output out_9
);

  wire and_1_out, full_adder_1_carry_out, full_adder_2_carry_out, half_adder_1_carry_out, or_1_out, or_2_out;
  wire [3:0] half_adder_1_sum_out;

  or or_1 (or_1_out, in_2, in_1);
  and and_1 (and_1_out, in_3, or_1_out);
  or or_2 (or_2_out, in_4, and_1_out);
  full_adder full_adder_1 (
    .in_1(1'b1), .in_2(in_2), .carry(half_adder_1_carry_out), .carry_out(full_adder_1_carry_out),
    .sum_out(half_adder_1_sum_out[1]));
  half_adder half_adder_1 (
    .in_1(1'b1), .in_2(in_1), .sum_out(half_adder_1_sum_out[0]), .carry_out(half_adder_1_carry_out));
  Multiplexer #(.width(4), .enable("false")) multiplexer_1 (
    .in0({in_4, in_3, in_2, in_1}), .in1(half_adder_1_sum_out), .out({out_9, out_8, out_7, out_6}),
    .sel(or_2_out));
  full_adder full_adder_2 (
    .in_1(1'b0), .in_2(in_3), .carry(full_adder_1_carry_out), .carry_out(full_adder_2_carry_out),
    .sum_out(half_adder_1_sum_out[2]));
  full_adder full_adder_3 (
    .in_1(1'b0), .in_2(in_4), .carry(full_adder_2_carry_out), .carry_out(Overflow),
    .sum_out(half_adder_1_sum_out[3]));
endmodule

module _4bitdisplay (
  input  a,
  input  b,
  input  c,
  input  d,
  output out_5,
  output out_6,
  output out_7,
  output out_8,
  output out_9,
  output out_10,
  output out_11,
  output out_12
);

  wire and_1_out, and_2_out, and_3_out, and_4_out, and_5_out, and_6_out, and_7_out, and_8_out, and_9_out,
       and_10_out, and_11_out, and_12_out, and_13_out, and_14_out, and_15_out, and_16_out, and_17_out,
       and_18_out, and_19_out, and_20_out, and_21_out, and_22_out, and_23_out, and_24_out, and_25_out,
       and_26_out, not_1_out, not_2_out, not_3_out, not_4_out, not_5_out, not_6_out, not_7_out, not_8_out,
       not_9_out, not_10_out, not_11_out, not_12_out, not_13_out, not_14_out, not_15_out, not_16_out,
       not_17_out, not_18_out, not_19_out, not_20_out, not_21_out, not_22_out, not_23_out, not_24_out,
       not_25_out, not_26_out, not_27_out, not_28_out, not_29_out, not_30_out, not_31_out, not_32_out,
       not_33_out, not_34_out, not_35_out, not_36_out, not_37_out, not_38_out, not_39_out, not_40_out,
       not_41_out, not_42_out, not_43_out, not_44_out, not_45_out, not_46_out, not_47_out, not_48_out,
       not_49_out, not_50_out, not_51_out, not_52_out, not_53_out;

  not not_1 (not_1_out, a);
  not not_2 (not_2_out, b);
  and and_1 (and_1_out, not_1_out, not_2_out, c);
  not not_3 (not_3_out, a);
  and and_2 (and_2_out, not_3_out, b, not_4_out);
  not not_4 (not_4_out, c);
  not not_5 (not_5_out, a);
  and and_3 (and_3_out, not_5_out, b, not_6_out);
  not not_6 (not_6_out, d);
  not not_7 (not_7_out, b);
  and and_4 (and_4_out, a, not_7_out, not_8_out);
  not not_8 (not_8_out, c);
  not not_9 (not_9_out, a);
  not not_10 (not_10_out, c);
  and and_5 (and_5_out, not_9_out, not_10_out, not_11_out);
  not not_11 (not_11_out, d);
  not not_12 (not_12_out, a);
  and and_6 (and_6_out, not_12_out, b, not_13_out);
  not not_13 (not_13_out, c);
  not not_14 (not_14_out, a);
  and and_7 (and_7_out, not_14_out, b, not_15_out);
  not not_15 (not_15_out, d);
  not not_16 (not_16_out, b);
  and and_8 (and_8_out, a, not_16_out, not_17_out);
  not not_17 (not_17_out, c);
  not not_18 (not_18_out, a);
  not not_19 (not_19_out, b);
  and and_9 (and_9_out, not_18_out, not_19_out, not_20_out);
  not not_20 (not_20_out, d);
  not not_21 (not_21_out, a);
  and and_10 (and_10_out, not_21_out, c);
  not not_22 (not_22_out, a);
  and and_11 (and_11_out, not_22_out, b, d);
  not not_23 (not_23_out, b);
  and and_12 (and_12_out, a, not_23_out, not_24_out);
  not not_24 (not_24_out, c);
  not not_25 (not_25_out, a);
  and and_13 (and_13_out, not_25_out, not_26_out);
  not not_26 (not_26_out, b);
  not not_27 (not_27_out, a);
  not not_28 (not_28_out, c);
  and and_14 (and_14_out, not_27_out, not_28_out, not_29_out);
  not not_29 (not_29_out, d);
  not not_30 (not_30_out, b);
  and and_15 (and_15_out, not_30_out, not_31_out);
  not not_31 (not_31_out, c);
  not not_32 (not_32_out, a);
  and and_16 (and_16_out, not_32_out, c, d);
  not not_33 (not_33_out, a);
  not not_34 (not_34_out, b);
  and and_17 (and_17_out, not_33_out, not_34_out, not_35_out);
  not not_35 (not_35_out, d);
  not not_36 (not_36_out, b);
  not not_37 (not_37_out, c);
  and and_18 (and_18_out, not_36_out, not_37_out, not_38_out);
  not not_38 (not_38_out, d);
  not not_39 (not_39_out, a);
  and and_19 (and_19_out, not_39_out, c, not_40_out);
  not not_40 (not_40_out, d);
  not not_41 (not_41_out, b);
  not not_42 (not_42_out, c);
  not not_43 (not_43_out, d);
  not not_44 (not_44_out, a);
  not not_45 (not_45_out, b);
  not not_46 (not_46_out, a);
  not not_47 (not_47_out, d);
  not not_48 (not_48_out, a);
  not not_49 (not_49_out, c);
  not not_50 (not_50_out, b);
  and and_20 (and_20_out, not_50_out, not_51_out);
  not not_51 (not_51_out, c);
  not not_52 (not_52_out, a);
  and and_21 (and_21_out, not_52_out, d);
  not not_53 (not_53_out, a);
  and and_22 (and_22_out, not_53_out, b);
  or or_1 (out_5, and_1_out, and_2_out, and_3_out, and_4_out);
  or or_2 (out_6, and_5_out, and_6_out, and_7_out, and_8_out);
  or or_3 (out_7, and_9_out, and_10_out, and_11_out, and_12_out);
  or or_4 (out_8, and_13_out, and_14_out, and_15_out, and_16_out);
  or or_5 (out_9, and_17_out, and_18_out, and_19_out);
  and and_23 (and_23_out, not_41_out, not_42_out, not_43_out);
  and and_24 (and_24_out, not_44_out, not_45_out, c);
  and and_25 (and_25_out, not_46_out, c, not_47_out);
  and and_26 (and_26_out, not_48_out, b, not_49_out, d);
  or or_6 (out_11, and_20_out, and_21_out, and_22_out);
  or or_7 (out_10, and_23_out, and_24_out, and_25_out, and_26_out);

  assign out_12 = 1'b0;
endmodule

module _2bitdisplay (
  input  a,
  input  b,
  output s1,
  output s2,
  output s3,
  output s4,
  output s5,
  output s6,
  output s7,
  output s8
);

  wire not_1_out, not_2_out, not_3_out, not_5_out, not_6_out;

  not not_1 (not_1_out, b);
  not not_2 (not_2_out, a);
  not not_3 (not_3_out, b);
  not not_4 (s3, b);
  not not_5 (not_5_out, a);
  not not_6 (not_6_out, b);
  not not_7 (s5, b);
  not not_8 (s6, b);
  not not_9 (s7, a);
  and and_1 (s1, a, not_1_out);
  and and_2 (s2, not_2_out, not_3_out);
  or or_1 (s4, not_5_out, not_6_out);

  assign s8 = 1'b0;
endmodule

module _8_bit_async_reg (
  input  [7:0] in_1,
  output [7:0] out_2
);

  D_Flip_Flop #(.trigger("high")) d_ff_1 (.clk(1'b1), .D(in_1[7]), .Q(out_2[7]));  // open: Qn, preset, en, reset
  D_Flip_Flop #(.trigger("high")) d_ff_2 (.clk(1'b1), .D(in_1[6]), .Q(out_2[6]));  // open: Qn, preset, en, reset
  D_Flip_Flop #(.trigger("high")) d_ff_3 (.clk(1'b1), .D(in_1[5]), .Q(out_2[5]));  // open: Qn, preset, en, reset
  D_Flip_Flop #(.trigger("high")) d_ff_4 (.clk(1'b1), .D(in_1[4]), .Q(out_2[4]));  // open: Qn, preset, en, reset
  D_Flip_Flop #(.trigger("high")) d_ff_5 (.clk(1'b1), .D(in_1[3]), .Q(out_2[3]));  // open: Qn, preset, en, reset
  D_Flip_Flop #(.trigger("high")) d_ff_6 (.clk(1'b1), .D(in_1[2]), .Q(out_2[2]));  // open: Qn, preset, en, reset
  D_Flip_Flop #(.trigger("high")) d_ff_7 (.clk(1'b1), .D(in_1[1]), .Q(out_2[1]));  // open: Qn, preset, en, reset
  D_Flip_Flop #(.trigger("high")) d_ff_8 (.clk(1'b1), .D(in_1[0]), .Q(out_2[0]));  // open: Qn, preset, en, reset
endmodule

module _4_bit_async_reg (
  input  [3:0] in_1,
  output [3:0] out_2
);

  D_Flip_Flop #(.trigger("high")) d_ff_1 (.clk(1'b1), .D(in_1[2]), .Q(out_2[2]));  // open: Qn, preset, en, reset
  D_Flip_Flop #(.trigger("high")) d_ff_2 (.clk(1'b1), .D(in_1[3]), .Q(out_2[3]));  // open: Qn, preset, en, reset
  D_Flip_Flop #(.trigger("high")) d_ff_3 (.clk(1'b1), .D(in_1[1]), .Q(out_2[1]));  // open: Qn, preset, en, reset
  D_Flip_Flop #(.trigger("high")) d_ff_4 (.clk(1'b1), .D(in_1[0]), .Q(out_2[0]));  // open: Qn, preset, en, reset
endmodule

module control_unit (
  input  Branch_Test,
  input  clock,
  input  [7:0] in_3,
  output tick_2,
  output stop,
  output tick_1,
  output tick_0,
  output Jump,
  output [1:0] out_9,
  output sys__mbr,
  output Mode,
  output out_12,
  output out_13,
  output pc__mar,
  output print,
  output inc,
  output [1:0] select_read_from_cpu_bus,
  output [1:0] select_write_to_cpu_bus
);

  wire and_1_out, and_2_out, and_3_out, and_4_out, and_5_out, and_7_out, and_10_out, and_12_out, and_13_out,
       and_14_out, decoder_1_out0, decoder_1_out1, decoder_1_out2, decoder_1_out3, L_S_out, not_1_out,
       not_2_out, not_3_out, not_4_out, not_5_out, not_6_out, not_7_out, not_8_out, not_9_out, not_10_out,
       not_11_out, not_12_out, not_13_out, not_14_out, or_5_out, P_I_2_out, P_I_out, Print_out, Save_out,
       xor_1_out;
  wire [1:0] micro_counter_2_sum, Micro_counter_out_3;

  or or_1 (Jump, and_2_out, and_1_out);
  and and_1 (and_1_out, decoder_1_out3, in_3[4], in_3[5]);
  and and_2 (and_2_out, xor_1_out, decoder_1_out2);
  not not_1 (not_1_out, in_3[5]);
  not not_2 (not_2_out, in_3[4]);
  and P_I (P_I_out, decoder_1_out3, not_1_out, not_2_out, in_3[3]);
  or ALU (select_write_to_cpu_bus[1], P_I_out, decoder_1_out1, L_S_out);
  xor xor_1 (xor_1_out, Branch_Test, in_3[5]);
  and Input (out_9[1], decoder_1_out3, not_3_out, in_3[4], not_14_out);
  not not_3 (not_3_out, in_3[5]);
  and L_S (L_S_out, in_3[4], in_3[5], decoder_1_out0);
  and and_3 (and_3_out, in_3[5], decoder_1_out0);
  not not_4 (not_4_out, decoder_1_out1);
  and and_4 (and_4_out, not_4_out, and_3_out);
  or or_2 (select_write_to_cpu_bus[0], and_4_out, and_5_out);
  or or_3 (out_9[0], Save_out, Print_out);
  and Save (Save_out, in_3[5], decoder_1_out0, not_14_out);
  and u_Print (Print_out, decoder_1_out3, not_14_out, not_3_out, and_14_out);
  and and_5 (and_5_out, decoder_1_out3, and_14_out);
  and and_6 (inc, in_3[2], decoder_1_out1);
  and and_7 (and_7_out, in_3[4], decoder_1_out0);
  and and_8 (tick_2, Micro_counter_out_3[1], clock, not_5_out);
  not not_5 (not_5_out, Micro_counter_out_3[0]);
  _2_bit_register Micro_counter (.CU_input(clock), .in_2(micro_counter_2_sum), .out_3(Micro_counter_out_3));
  // Probe on Micro_counter_out_3
  and P_I_2 (P_I_2_out, decoder_1_out3, in_3[4], in_3[3]);
  or or_4 (select_read_from_cpu_bus[1], and_7_out, P_I_2_out, and_10_out);
  and and_9 (tick_1, not_6_out, clock, Micro_counter_out_3[0]);
  not not_6 (not_6_out, Micro_counter_out_3[1]);
  micro_counter micro_counter_2 (.in_1(Micro_counter_out_3), .Sum(micro_counter_2_sum));
  and and_10 (and_10_out, decoder_1_out1, in_3[3]);
  and and_11 (pc__mar, not_8_out, not_7_out);
  not not_7 (not_7_out, Micro_counter_out_3[0]);
  not not_8 (not_8_out, Micro_counter_out_3[1]);
  not not_9 (not_9_out, in_3[5]);
  and and_12 (and_12_out, not_9_out, tick_1, or_5_out);
  or or_5 (or_5_out, decoder_1_out0, out_9[1]);
  not not_10 (not_10_out, in_3[5]);
  and and_13 (and_13_out, decoder_1_out0, not_10_out);
  or or_6 (select_read_from_cpu_bus[0], and_13_out, out_9[1], decoder_1_out1);
  or or_7 (sys__mbr, pc__mar, and_12_out);
  not not_11 (not_11_out, in_3[4]);
  not not_12 (not_12_out, in_3[5]);
  and and_14 (and_14_out, not_11_out, not_12_out, decoder_1_out3);
  not not_13 (not_13_out, in_3[4]);
  not not_14 (not_14_out, pc__mar);
  and and_15 (stop, not_13_out, in_3[5], decoder_1_out3);
  Decoder #(.select(2), .enable("false")) decoder_1 (
    .out0(decoder_1_out0), .out1(decoder_1_out1), .out2(decoder_1_out2), .out3(decoder_1_out3),
    .sel(in_3[7:6]));
  and and_16 (Mode, tick_1, decoder_1_out0, in_3[5]);
  and and_17 (print, and_14_out, tick_2);

  assign out_12 = in_3[5];
  assign out_13 = in_3[4];
  assign tick_0 = pc__mar;

  // Notes on the sheet:
  //   00 = DR, 01 = MBR -> sys bus
  //   L/S
  //   ALU
  //   L/S
  //   ALU
endmodule

module inputbuffer (
  input  _0,
  input  _1,
  input  _2,
  input  _3,
  input  _4,
  input  _5,
  input  _6,
  input  _7,
  input  _8,
  input  _9,
  output [7:0] out_11
);

  wire [7:0] multiplexer_1_out, multiplexer_2_out, multiplexer_3_out, multiplexer_4_out, multiplexer_5_out,
       multiplexer_6_out, multiplexer_7_out, multiplexer_8_out, multiplexer_9_out, multiplexer_10_out,
       or_1_out;

  Multiplexer #(.width(8), .disabled(0), .enable("false")) multiplexer_1 (
    .in0({8{1'b0}}), .in1({8{1'b0}}), .out(multiplexer_1_out), .sel(_0));
  Multiplexer #(.width(8), .disabled(0), .enable("false")) multiplexer_2 (
    .in0({8{1'b0}}), .in1(8'h1), .out(multiplexer_2_out), .sel(_1));
  Multiplexer #(.width(8), .disabled(0), .enable("false")) multiplexer_3 (
    .in0({8{1'b0}}), .in1(8'h2), .out(multiplexer_3_out), .sel(_2));
  Multiplexer #(.width(8), .disabled(0), .enable("false")) multiplexer_4 (
    .in0({8{1'b0}}), .in1(8'h3), .out(multiplexer_4_out), .sel(_3));
  Multiplexer #(.width(8), .disabled(0), .enable("false")) multiplexer_5 (
    .in0({8{1'b0}}), .in1(8'h4), .out(multiplexer_5_out), .sel(_4));
  Multiplexer #(.width(8), .disabled(0), .enable("false")) multiplexer_6 (
    .in0({8{1'b0}}), .in1(8'h5), .out(multiplexer_6_out), .sel(_5));
  Multiplexer #(.width(8), .disabled(0), .enable("false")) multiplexer_7 (
    .in0({8{1'b0}}), .in1(8'h6), .out(multiplexer_7_out), .sel(_6));
  Multiplexer #(.width(8), .disabled(0), .enable("false")) multiplexer_8 (
    .in0({8{1'b0}}), .in1(8'h7), .out(multiplexer_8_out), .sel(_7));
  Multiplexer #(.width(8), .disabled(0), .enable("false")) multiplexer_9 (
    .in0({8{1'b0}}), .in1(8'h8), .out(multiplexer_9_out), .sel(_8));
  Multiplexer #(.width(8), .disabled(0), .enable("false")) multiplexer_10 (
    .in0({8{1'b0}}), .in1(8'h9), .out(multiplexer_10_out), .sel(_9));
  assign or_1_out = multiplexer_1_out | multiplexer_2_out | multiplexer_3_out | multiplexer_4_out | multiplexer_5_out | multiplexer_6_out | multiplexer_7_out | multiplexer_8_out | multiplexer_9_out | multiplexer_10_out;  // OR_Gate or_1, 8 bits wide
  _8_bit_async_reg u_8_bit_async_reg_1 (.in_1(or_1_out), .out_2(out_11));
endmodule

module _1_bit_async_register (
  input  in_1,
  output out_2
);

  wire d_ff_1_qn, undriven, undriven_2, undriven_3;

  D_Flip_Flop #(.trigger("high")) d_ff_1 (
    .clk(1'b1), .D(in_1), .Q(out_2), .Qn(d_ff_1_qn), .preset(undriven), .en(undriven_2), .reset(undriven_3));
  D_Flip_Flop #(.trigger("high")) d_ff_2 (
    .clk(1'b1), .D(in_1), .Q(out_2), .Qn(d_ff_1_qn), .preset(undriven), .en(undriven_2), .reset(undriven_3));
endmodule

module _8_bit_adder (
  input  [7:0] in_1,
  input  [7:0] in_2,
  output out_3,
  output [7:0] out_4
);

  wire full_adder_1_carry_out, full_adder_2_carry_out, full_adder_3_carry_out, full_adder_4_carry_out,
       full_adder_5_carry_out, full_adder_6_carry_out, half_adder_1_carry_out;
  wire [7:0] n8_bit_async_reg_1_out_2, n8_bit_async_reg_2_out_2;

  _8_bit_async_reg u_8_bit_async_reg_1 (.in_1(in_1), .out_2(n8_bit_async_reg_1_out_2));
  _8_bit_async_reg u_8_bit_async_reg_2 (.in_1(in_2), .out_2(n8_bit_async_reg_2_out_2));
  full_adder full_adder_1 (
    .in_1(n8_bit_async_reg_1_out_2[4]), .in_2(n8_bit_async_reg_2_out_2[4]), .carry(full_adder_2_carry_out),
    .carry_out(full_adder_1_carry_out), .sum_out(out_4[4]));
  full_adder full_adder_2 (
    .in_1(n8_bit_async_reg_1_out_2[3]), .in_2(n8_bit_async_reg_2_out_2[3]), .carry(full_adder_3_carry_out),
    .carry_out(full_adder_2_carry_out), .sum_out(out_4[3]));
  full_adder full_adder_3 (
    .in_1(n8_bit_async_reg_1_out_2[2]), .in_2(n8_bit_async_reg_2_out_2[2]), .carry(full_adder_4_carry_out),
    .carry_out(full_adder_3_carry_out), .sum_out(out_4[2]));
  full_adder full_adder_4 (
    .in_1(n8_bit_async_reg_1_out_2[1]), .in_2(n8_bit_async_reg_2_out_2[1]), .carry(half_adder_1_carry_out),
    .carry_out(full_adder_4_carry_out), .sum_out(out_4[1]));
  half_adder half_adder_1 (
    .in_1(n8_bit_async_reg_1_out_2[0]), .in_2(n8_bit_async_reg_2_out_2[0]), .sum_out(out_4[0]),
    .carry_out(half_adder_1_carry_out));
  full_adder full_adder_5 (
    .in_1(n8_bit_async_reg_1_out_2[6]), .in_2(n8_bit_async_reg_2_out_2[6]), .carry(full_adder_6_carry_out),
    .carry_out(full_adder_5_carry_out), .sum_out(out_4[6]));
  full_adder full_adder_6 (
    .in_1(n8_bit_async_reg_1_out_2[5]), .in_2(n8_bit_async_reg_2_out_2[5]), .carry(full_adder_1_carry_out),
    .carry_out(full_adder_6_carry_out), .sum_out(out_4[5]));
  full_adder full_adder_7 (
    .in_1(n8_bit_async_reg_1_out_2[7]), .in_2(n8_bit_async_reg_2_out_2[7]), .carry(full_adder_5_carry_out),
    .carry_out(out_3), .sum_out(out_4[7]));
endmodule

module multiply (
  input  [7:0] in_1,
  input  in_2,
  output [7:0] out_3
);

  wire and_1_out, and_2_out, and_3_out, and_4_out, and_5_out, and_6_out, and_7_out, and_8_out, and_9_out,
       and_10_out, and_11_out, and_12_out, and_13_out, and_14_out, and_15_out, and_16_out, and_17_out,
       and_18_out, and_19_out, and_20_out, and_21_out, and_22_out, and_23_out, and_24_out, and_25_out,
       and_26_out, and_27_out, and_28_out, and_29_out, and_30_out, and_31_out, and_32_out, and_33_out,
       and_34_out, and_35_out, and_36_out, and_37_out, and_38_out, and_39_out, and_40_out, j_k_ff_1_q,
       j_k_ff_1_qn, j_k_ff_17_qn, not_1_out, not_2_out, not_3_out, not_4_out, not_5_out, not_6_out,
       not_7_out, not_8_out, not_9_out, not_10_out, not_11_out, not_12_out, not_13_out, not_14_out,
       not_15_out, not_16_out, not_17_out, or_1_out, or_2_out, or_3_out, or_4_out, or_5_out, or_6_out,
       or_7_out, or_8_out, or_9_out, or_10_out, or_11_out, or_12_out, or_13_out, or_14_out, or_15_out,
       or_16_out;
  wire [7:0] j_k_ff_16_q, n8_bit_adder_1_out_4, n8_bit_async_reg_1_out_2;

  J_K_Flip_Flop j_k_ff_1 (
    .J(in_2), .clk(in_2), .K(not_1_out), .Q(j_k_ff_1_q), .Qn(j_k_ff_1_qn));  // open: preset, en, reset
  not not_1 (not_1_out, in_2);
  _8_bit_async_reg u_8_bit_async_reg_1 (.in_1(in_1), .out_2(n8_bit_async_reg_1_out_2));
  and and_1 (and_1_out, n8_bit_adder_1_out_4[7], j_k_ff_1_qn, out_3[0]);
  and and_2 (and_2_out, 1'b0, j_k_ff_1_q);
  not not_2 (not_2_out, or_1_out);
  and and_3 (and_3_out, j_k_ff_1_qn, j_k_ff_17_qn, j_k_ff_16_q[7]);
  and and_4 (and_4_out, j_k_ff_16_q[0], j_k_ff_1_q);
  and and_5 (and_5_out, j_k_ff_1_qn, out_3[7]);
  or or_1 (or_1_out, and_1_out, and_3_out, and_2_out);
  J_K_Flip_Flop j_k_ff_2 (.J(or_1_out), .clk(in_2), .K(not_2_out), .Q(j_k_ff_16_q[7]));  // open: Qn, preset, en, reset
  or or_2 (or_2_out, and_5_out, and_4_out);
  J_K_Flip_Flop j_k_ff_3 (.J(or_2_out), .clk(in_2), .K(not_3_out), .Q(out_3[7]));  // open: Qn, preset, en, reset
  not not_3 (not_3_out, or_2_out);
  and and_6 (and_6_out, n8_bit_adder_1_out_4[6], j_k_ff_1_qn, out_3[0]);
  and and_7 (and_7_out, j_k_ff_16_q[7], j_k_ff_1_q);
  and and_8 (and_8_out, j_k_ff_1_qn, j_k_ff_17_qn, j_k_ff_16_q[6]);
  and and_9 (and_9_out, out_3[7], j_k_ff_1_q);
  and and_10 (and_10_out, j_k_ff_1_qn, out_3[6]);
  _8_bit_adder u_8_bit_adder_1 (
    .in_1(n8_bit_async_reg_1_out_2), .in_2(j_k_ff_16_q), .out_4(n8_bit_adder_1_out_4));  // open: out_3
  or or_3 (or_3_out, and_6_out, and_8_out, and_7_out);
  J_K_Flip_Flop j_k_ff_4 (.J(or_3_out), .clk(in_2), .K(not_4_out), .Q(j_k_ff_16_q[6]));  // open: Qn, preset, en, reset
  not not_4 (not_4_out, or_3_out);
  or or_4 (or_4_out, and_10_out, and_9_out);
  J_K_Flip_Flop j_k_ff_5 (.J(or_4_out), .clk(in_2), .K(not_5_out), .Q(out_3[6]));  // open: Qn, preset, en, reset
  not not_5 (not_5_out, or_4_out);
  and and_11 (and_11_out, n8_bit_adder_1_out_4[5], j_k_ff_1_qn, out_3[0]);
  and and_12 (and_12_out, j_k_ff_16_q[6], j_k_ff_1_q);
  and and_13 (and_13_out, j_k_ff_1_qn, j_k_ff_17_qn, j_k_ff_16_q[5]);
  and and_14 (and_14_out, out_3[6], j_k_ff_1_q);
  and and_15 (and_15_out, j_k_ff_1_qn, out_3[5]);
  or or_5 (or_5_out, and_11_out, and_13_out, and_12_out);
  J_K_Flip_Flop j_k_ff_6 (.J(or_5_out), .clk(in_2), .K(not_6_out), .Q(j_k_ff_16_q[5]));  // open: Qn, preset, en, reset
  not not_6 (not_6_out, or_5_out);
  or or_6 (or_6_out, and_15_out, and_14_out);
  J_K_Flip_Flop j_k_ff_7 (.J(or_6_out), .clk(in_2), .K(not_7_out), .Q(out_3[5]));  // open: Qn, preset, en, reset
  not not_7 (not_7_out, or_6_out);
  and and_16 (and_16_out, n8_bit_adder_1_out_4[4], j_k_ff_1_qn, out_3[0]);
  and and_17 (and_17_out, j_k_ff_16_q[5], j_k_ff_1_q);
  and and_18 (and_18_out, j_k_ff_1_qn, j_k_ff_17_qn, j_k_ff_16_q[4]);
  and and_19 (and_19_out, out_3[5], j_k_ff_1_q);
  and and_20 (and_20_out, j_k_ff_1_qn, out_3[4]);
  or or_7 (or_7_out, and_16_out, and_18_out, and_17_out);
  J_K_Flip_Flop j_k_ff_8 (.J(or_7_out), .clk(in_2), .K(not_8_out), .Q(j_k_ff_16_q[4]));  // open: Qn, preset, en, reset
  not not_8 (not_8_out, or_7_out);
  or or_8 (or_8_out, and_20_out, and_19_out);
  not not_9 (not_9_out, or_8_out);
  and and_21 (and_21_out, j_k_ff_16_q[4], j_k_ff_1_q);
  and and_22 (and_22_out, j_k_ff_1_qn, j_k_ff_17_qn, j_k_ff_16_q[3]);
  and and_23 (and_23_out, out_3[4], j_k_ff_1_q);
  J_K_Flip_Flop j_k_ff_9 (.J(or_8_out), .clk(in_2), .K(not_9_out), .Q(out_3[4]));  // open: Qn, preset, en, reset
  and and_24 (and_24_out, j_k_ff_1_qn, out_3[3]);
  and and_25 (and_25_out, n8_bit_adder_1_out_4[3], j_k_ff_1_qn, out_3[0]);
  or or_9 (or_9_out, and_25_out, and_22_out, and_21_out);
  not not_10 (not_10_out, or_9_out);
  or or_10 (or_10_out, and_24_out, and_23_out);
  not not_11 (not_11_out, or_10_out);
  and and_26 (and_26_out, j_k_ff_16_q[3], j_k_ff_1_q);
  J_K_Flip_Flop j_k_ff_10 (
    .J(or_9_out), .clk(in_2), .K(not_10_out), .Q(j_k_ff_16_q[3]));  // open: Qn, preset, en, reset
  and and_27 (and_27_out, j_k_ff_1_qn, j_k_ff_17_qn, j_k_ff_16_q[2]);
  and and_28 (and_28_out, out_3[3], j_k_ff_1_q);
  J_K_Flip_Flop j_k_ff_11 (.J(or_10_out), .clk(in_2), .K(not_11_out), .Q(out_3[3]));  // open: Qn, preset, en, reset
  and and_29 (and_29_out, j_k_ff_1_qn, out_3[2]);
  and and_30 (and_30_out, n8_bit_adder_1_out_4[2], j_k_ff_1_qn, out_3[0]);
  or or_11 (or_11_out, and_30_out, and_27_out, and_26_out);
  not not_12 (not_12_out, or_11_out);
  not not_13 (not_13_out, or_12_out);
  and and_31 (and_31_out, j_k_ff_16_q[2], j_k_ff_1_q);
  J_K_Flip_Flop j_k_ff_12 (
    .J(or_11_out), .clk(in_2), .K(not_12_out), .Q(j_k_ff_16_q[2]));  // open: Qn, preset, en, reset
  and and_32 (and_32_out, j_k_ff_1_qn, j_k_ff_17_qn, j_k_ff_16_q[1]);
  or or_12 (or_12_out, and_29_out, and_28_out);
  and and_33 (and_33_out, out_3[2], j_k_ff_1_q);
  J_K_Flip_Flop j_k_ff_13 (.J(or_12_out), .clk(in_2), .K(not_13_out), .Q(out_3[2]));  // open: Qn, preset, en, reset
  and and_34 (and_34_out, j_k_ff_1_qn, out_3[1]);
  and and_35 (and_35_out, n8_bit_adder_1_out_4[1], j_k_ff_1_qn, out_3[0]);
  not not_14 (not_14_out, or_13_out);
  not not_15 (not_15_out, or_14_out);
  or or_13 (or_13_out, and_35_out, and_32_out, and_31_out);
  and and_36 (and_36_out, j_k_ff_16_q[1], j_k_ff_1_q);
  J_K_Flip_Flop j_k_ff_14 (
    .J(or_13_out), .clk(in_2), .K(not_14_out), .Q(j_k_ff_16_q[1]));  // open: Qn, preset, en, reset
  and and_37 (and_37_out, j_k_ff_1_qn, j_k_ff_17_qn, j_k_ff_16_q[0]);
  or or_14 (or_14_out, and_34_out, and_33_out);
  J_K_Flip_Flop j_k_ff_15 (.J(or_14_out), .clk(in_2), .K(not_15_out), .Q(out_3[1]));  // open: Qn, preset, en, reset
  and and_38 (and_38_out, n8_bit_adder_1_out_4[0], j_k_ff_1_qn, out_3[0]);
  not not_16 (not_16_out, or_15_out);
  and and_39 (and_39_out, out_3[1], j_k_ff_1_q);
  not not_17 (not_17_out, or_16_out);
  and and_40 (and_40_out, j_k_ff_1_qn, out_3[0]);
  or or_15 (or_15_out, and_38_out, and_37_out, and_36_out);
  J_K_Flip_Flop j_k_ff_16 (
    .J(or_15_out), .clk(in_2), .K(not_16_out), .Q(j_k_ff_16_q[0]));  // open: Qn, preset, en, reset
  or or_16 (or_16_out, and_40_out, and_39_out);
  J_K_Flip_Flop j_k_ff_17 (
    .J(or_16_out), .clk(in_2), .K(not_17_out), .Q(out_3[0]), .Qn(j_k_ff_17_qn));  // open: preset, en, reset

  // Notes on the sheet:
  //   shift
  //   Register
endmodule

module _4bit_control_buffer (
  input  [3:0] in_1,
  input  clock,
  output [3:0] out_3
);

  Multiplexer #(.width(4)) multiplexer_1 (.in0(in_1), .out(out_3), .sel(1'b0), .en(clock));  // open: in1
endmodule

module _8bit_control_buffer (
  input  [7:0] in_1,
  input  control_input,
  output [7:0] out_3
);

  Multiplexer #(.width(8)) multiplexer_1 (.in0(in_1), .out(out_3), .sel(1'b0), .en(control_input));  // open: in1
endmodule

module micro_counter (
  input  [1:0] in_1,
  output [1:0] Sum
);

  wire full_adder_1_carry_out, half_adder_1_carry_out;

  half_adder half_adder_1 (.in_1(1'b1), .in_2(in_1[0]), .sum_out(Sum[0]), .carry_out(half_adder_1_carry_out));
  full_adder full_adder_1 (
    .in_1(1'b0), .in_2(in_1[1]), .carry(half_adder_1_carry_out), .carry_out(full_adder_1_carry_out),
    .sum_out(Sum[1]));
endmodule

module _2_bit_register (
  input  CU_input,
  input  [1:0] in_2,
  output [1:0] out_3
);

  D_Flip_Flop #(.trigger("falling")) d_ff_1 (.clk(CU_input), .D(in_2[0]), .Q(out_3[0]));  // open: Qn, preset, en, reset
  D_Flip_Flop #(.trigger("falling")) d_ff_2 (.clk(CU_input), .D(in_2[1]), .Q(out_3[1]));  // open: Qn, preset, en, reset
endmodule

module _1_bit_control_buffer (
  input  in_1,
  input  control_input,
  output out_3
);

  Multiplexer #(.disabled(0)) multiplexer_1 (.in0(in_1), .out(out_3), .sel(1'b0), .en(control_input));  // open: in1
endmodule

module _4bit_rising_reg (
  input  CU_input,
  input  [3:0] in_2,
  output [3:0] out_3
);

  D_Flip_Flop #(.trigger("falling")) d_ff_1 (.clk(CU_input), .D(in_2[2]), .Q(out_3[2]));  // open: Qn, preset, en, reset
  D_Flip_Flop #(.trigger("falling")) d_ff_2 (.clk(CU_input), .D(in_2[3]), .Q(out_3[3]));  // open: Qn, preset, en, reset
  D_Flip_Flop #(.trigger("falling")) d_ff_3 (.clk(CU_input), .D(in_2[1]), .Q(out_3[1]));  // open: Qn, preset, en, reset
  D_Flip_Flop #(.trigger("falling")) d_ff_4 (.clk(CU_input), .D(in_2[0]), .Q(out_3[0]));  // open: Qn, preset, en, reset
endmodule

module _8bit_rising_reg (
  input  clock_input,
  input  [7:0] in_2,
  output [7:0] out_3
);

  D_Flip_Flop d_ff_1 (.clk(clock_input), .D(in_2[6]), .Q(out_3[6]));  // open: Qn, preset, en, reset
  D_Flip_Flop d_ff_2 (.clk(clock_input), .D(in_2[7]), .Q(out_3[7]));  // open: Qn, preset, en, reset
  D_Flip_Flop d_ff_3 (.clk(clock_input), .D(in_2[5]), .Q(out_3[5]));  // open: Qn, preset, en, reset
  D_Flip_Flop d_ff_4 (.clk(clock_input), .D(in_2[4]), .Q(out_3[4]));  // open: Qn, preset, en, reset
  D_Flip_Flop d_ff_5 (.clk(clock_input), .D(in_2[3]), .Q(out_3[3]));  // open: Qn, preset, en, reset
  D_Flip_Flop d_ff_6 (.clk(clock_input), .D(in_2[2]), .Q(out_3[2]));  // open: Qn, preset, en, reset
  D_Flip_Flop d_ff_7 (.clk(clock_input), .D(in_2[1]), .Q(out_3[1]));  // open: Qn, preset, en, reset
  D_Flip_Flop d_ff_8 (.clk(clock_input), .D(in_2[0]), .Q(out_3[0]));  // open: Qn, preset, en, reset
endmodule

module _8bit_adder (
  input  PLA_input,
  input  in_2,
  input  in_3,
  input  in_4,
  input  in_5,
  input  in_6,
  input  in_7,
  input  in_8,
  input  in_9,
  input  in_10,
  input  in_11,
  input  in_12,
  input  in_13,
  input  in_14,
  input  in_15,
  input  in_16,
  input  in_17,
  output out_18,
  output out_19,
  output out_20,
  output out_21,
  output out_22,
  output out_23,
  output out_24,
  output out_25,
  output out_26,
  output Zero_output_flag
);

  wire and_1_out, and_2_out, and_3_out, and_4_out, and_5_out, and_6_out, and_7_out, and_8_out, and_9_out,
       and_10_out, and_11_out, and_12_out, and_13_out, and_14_out, and_15_out, and_16_out, and_18_out,
       full_adder_1_carry, full_adder_3_carry, full_adder_4_carry, full_adder_5_carry, full_adder_6_carry,
       full_adder_7_carry, half_adder_1_carry, not_1_out, not_2_out, not_3_out, not_4_out, not_5_out,
       not_6_out, not_7_out, not_8_out;

  and and_1 (and_1_out, PLA_input, in_10);
  and and_2 (and_2_out, PLA_input, in_11);
  and and_3 (and_3_out, PLA_input, in_12);
  and and_4 (and_4_out, PLA_input, in_13);
  and and_5 (and_5_out, PLA_input, in_14);
  and and_6 (and_6_out, in_15, PLA_input);
  and and_7 (and_7_out, PLA_input, in_16);
  and and_8 (and_8_out, PLA_input, in_17);
  and and_9 (and_9_out, PLA_input, in_2);
  and and_10 (and_10_out, PLA_input, in_3);
  Full_Adder full_adder_1 (
    .in_1(and_10_out), .in_2(and_2_out), .in_3(full_adder_3_carry), .carry(full_adder_1_carry), .sum(out_20));
  Full_Adder full_adder_2 (.in_1(and_9_out), .in_2(and_1_out), .in_3(full_adder_1_carry), .carry(out_18), .sum(out_19));
  and and_11 (and_11_out, PLA_input, in_4);
  Full_Adder full_adder_3 (
    .in_1(and_11_out), .in_2(and_3_out), .in_3(full_adder_4_carry), .carry(full_adder_3_carry), .sum(out_21));
  and and_12 (and_12_out, in_5, PLA_input);
  Full_Adder full_adder_4 (
    .in_1(and_12_out), .in_2(and_4_out), .in_3(full_adder_5_carry), .carry(full_adder_4_carry), .sum(out_22));
  and and_13 (and_13_out, in_7, PLA_input);
  and and_14 (and_14_out, in_6, PLA_input);
  Full_Adder full_adder_5 (
    .in_1(and_14_out), .in_2(and_5_out), .in_3(full_adder_6_carry), .carry(full_adder_5_carry), .sum(out_23));
  Full_Adder full_adder_6 (
    .in_1(and_13_out), .in_2(and_6_out), .in_3(full_adder_7_carry), .carry(full_adder_6_carry), .sum(out_24));
  and and_15 (and_15_out, in_8, PLA_input);
  Full_Adder full_adder_7 (
    .in_1(and_15_out), .in_2(and_7_out), .in_3(half_adder_1_carry), .carry(full_adder_7_carry), .sum(out_25));
  and and_16 (and_16_out, in_9, PLA_input);
  Half_Adder half_adder_1 (.in_1(and_16_out), .in_2(and_8_out), .sum(out_26), .carry(half_adder_1_carry));
  not not_1 (not_1_out, out_22);
  not not_2 (not_2_out, out_21);
  not not_3 (not_3_out, out_19);
  not not_4 (not_4_out, out_20);
  and and_17 (Zero_output_flag, PLA_input, and_18_out);
  not not_5 (not_5_out, out_25);
  not not_6 (not_6_out, out_23);
  not not_7 (not_7_out, out_24);
  not not_8 (not_8_out, out_26);
  and and_18 (and_18_out, not_3_out, not_4_out, not_2_out, not_1_out, not_6_out, not_7_out, not_5_out, not_8_out);

  // Notes on the sheet:
  //   L
  //   Overflow Status
  //   L2
  //   R2
  //   L1
  //   L0
  //   R1
  //   R0
  //   R
  //   A-Out
endmodule

module Half_Adder (
  input  in_1,
  input  in_2,
  output sum,
  output carry
);

  wire not_1_out, or_1_out;

  or or_1 (or_1_out, in_1, in_2);
  and and_1 (carry, in_1, in_2);
  not not_1 (not_1_out, carry);
  and and_2 (sum, or_1_out, not_1_out);
endmodule

module Full_Adder (
  input  in_1,
  input  in_2,
  input  in_3,
  output carry,
  output sum
);

  wire half_adder_1_carry, half_adder_1_sum, half_adder_2_carry;

  Half_Adder half_adder_1 (.in_1(in_1), .in_2(in_2), .sum(half_adder_1_sum), .carry(half_adder_1_carry));
  Half_Adder half_adder_2 (.in_1(half_adder_1_sum), .in_2(in_3), .sum(sum), .carry(half_adder_2_carry));
  or or_1 (carry, half_adder_1_carry, half_adder_2_carry);
endmodule

module ALU (
  input  in_1,
  input  in_2,
  input  [7:0] in_3,
  input  [7:0] in_4,
  output neg_output,
  output out_6,
  output out_7,
  output out_8,
  output out_9,
  output out_10,
  output out_11,
  output out_12,
  output out_13,
  output zero_output,
  output overflow_output
);

  wire _8BIT_ADDER_ADD_out_18, _8BIT_ADDER_ADD_out_19, _8BIT_ADDER_ADD_out_20, _8BIT_ADDER_ADD_out_21,
       _8BIT_ADDER_ADD_out_22, _8BIT_ADDER_ADD_out_23, _8BIT_ADDER_ADD_out_24, _8BIT_ADDER_ADD_out_25,
       _8BIT_ADDER_ADD_out_26, _8BIT_ADDER_ADD_zero_output_flag, _8BIT_ADDER_SUB_out_18,
       _8BIT_ADDER_SUB_out_20, _8BIT_ADDER_SUB_out_21, _8BIT_ADDER_SUB_out_22, _8BIT_ADDER_SUB_out_23,
       _8BIT_ADDER_SUB_out_24, _8BIT_ADDER_SUB_out_25, _8BIT_ADDER_SUB_out_26,
       _8BIT_ADDER_SUB_zero_output_flag, and_1_out, and_2_out, not_1_out, not_2_out;

  not not_1 (not_1_out, in_1);
  not not_2 (not_2_out, in_2);
  and and_1 (and_1_out, in_2, not_1_out);
  _8bit_adder _8BIT_ADDER_SUB (
    .PLA_input(and_1_out), .in_10(in_3[7]), .in_11(in_3[6]), .in_12(in_3[5]), .in_13(in_3[4]),
    .in_14(in_3[3]), .in_15(in_3[2]), .in_16(in_3[1]), .in_17(in_3[0]), .in_2(in_4[7]), .in_3(in_4[6]),
    .in_4(in_4[5]), .in_5(in_4[4]), .in_6(in_4[3]), .in_7(in_4[2]), .in_8(in_4[1]), .in_9(in_4[0]),
    .out_18(_8BIT_ADDER_SUB_out_18), .Zero_output_flag(_8BIT_ADDER_SUB_zero_output_flag),
    .out_19(neg_output), .out_20(_8BIT_ADDER_SUB_out_20), .out_21(_8BIT_ADDER_SUB_out_21),
    .out_22(_8BIT_ADDER_SUB_out_22), .out_23(_8BIT_ADDER_SUB_out_23), .out_24(_8BIT_ADDER_SUB_out_24),
    .out_25(_8BIT_ADDER_SUB_out_25), .out_26(_8BIT_ADDER_SUB_out_26));
  or or_1 (out_6, neg_output, _8BIT_ADDER_ADD_out_19);
  or or_2 (out_7, _8BIT_ADDER_SUB_out_20, _8BIT_ADDER_ADD_out_20);
  or or_3 (out_8, _8BIT_ADDER_SUB_out_21, _8BIT_ADDER_ADD_out_21);
  and and_2 (and_2_out, not_2_out, not_1_out);
  _8bit_adder _8BIT_ADDER_ADD (
    .PLA_input(and_2_out), .in_10(in_3[7]), .in_11(in_3[6]), .in_12(in_3[5]), .in_13(in_3[4]),
    .in_14(in_3[3]), .in_15(in_3[2]), .in_16(in_3[1]), .in_17(in_3[0]), .in_2(in_4[7]), .in_3(in_4[6]),
    .in_4(in_4[5]), .in_5(in_4[4]), .in_6(in_4[3]), .in_7(in_4[2]), .in_8(in_4[1]), .in_9(in_4[0]),
    .out_18(_8BIT_ADDER_ADD_out_18), .Zero_output_flag(_8BIT_ADDER_ADD_zero_output_flag),
    .out_19(_8BIT_ADDER_ADD_out_19), .out_20(_8BIT_ADDER_ADD_out_20), .out_21(_8BIT_ADDER_ADD_out_21),
    .out_22(_8BIT_ADDER_ADD_out_22), .out_23(_8BIT_ADDER_ADD_out_23), .out_24(_8BIT_ADDER_ADD_out_24),
    .out_25(_8BIT_ADDER_ADD_out_25), .out_26(_8BIT_ADDER_ADD_out_26));
  or or_4 (out_9, _8BIT_ADDER_SUB_out_22, _8BIT_ADDER_ADD_out_22);
  or or_5 (out_10, _8BIT_ADDER_SUB_out_23, _8BIT_ADDER_ADD_out_23);
  or or_6 (out_11, _8BIT_ADDER_ADD_out_24, _8BIT_ADDER_SUB_out_24);
  or or_7 (overflow_output, _8BIT_ADDER_SUB_out_18, _8BIT_ADDER_ADD_out_18);
  or or_8 (out_12, _8BIT_ADDER_SUB_out_25, _8BIT_ADDER_ADD_out_25);
  or or_9 (zero_output, _8BIT_ADDER_ADD_zero_output_flag, _8BIT_ADDER_SUB_zero_output_flag);
  or or_10 (out_13, _8BIT_ADDER_SUB_out_26, _8BIT_ADDER_ADD_out_26);
endmodule

module dummy_box (
  input  PLA_INPUT,
  input  A0,
  input  B0,
  input  A1,
  input  B1,
  input  A2,
  input  B2,
  input  A3,
  input  B3,
  input  A4,
  input  B4,
  input  A5,
  input  B5,
  input  A6,
  input  B6,
  input  A7,
  input  B7,
  output R0,
  output R1,
  output R2,
  output R3,
  output R4,
  output R5,
  output R6,
  output R7
);

  wire and_1_out, and_2_out, and_3_out, and_4_out, and_5_out, and_6_out, and_7_out, and_8_out, and_9_out,
       and_10_out, and_11_out, and_12_out, and_13_out, and_14_out, and_15_out, and_16_out;

  and and_1 (and_1_out, A0, PLA_INPUT);
  and and_2 (and_2_out, B0, PLA_INPUT);
  and and_3 (and_3_out, A1, PLA_INPUT);
  and and_4 (and_4_out, B1, PLA_INPUT);
  and and_5 (and_5_out, A2, PLA_INPUT);
  and and_6 (and_6_out, B2, PLA_INPUT);
  and and_7 (and_7_out, A3, PLA_INPUT);
  and and_8 (and_8_out, B3, PLA_INPUT);
  and and_9 (and_9_out, A4, PLA_INPUT);
  and and_10 (and_10_out, B4, PLA_INPUT);
  and and_11 (and_11_out, A5, PLA_INPUT);
  and and_12 (and_12_out, B5, PLA_INPUT);
  and and_13 (and_13_out, A6, PLA_INPUT);
  and and_14 (and_14_out, B6, PLA_INPUT);
  and and_15 (and_15_out, A7, PLA_INPUT);
  and and_16 (and_16_out, B7, PLA_INPUT);
  or or_1 (R0, and_1_out, and_2_out);
  or or_2 (R1, and_3_out, and_4_out);
  or or_3 (R2, and_5_out, and_6_out);
  or or_4 (R3, and_7_out, and_8_out);
  or or_5 (R4, and_9_out, and_10_out);
  or or_6 (R5, and_11_out, and_12_out);
  or or_7 (R6, and_13_out, and_14_out);
  or or_8 (R7, and_15_out, and_16_out);
endmodule

module _2_s_Complement (
  input  in_1,
  input  in_2,
  input  [7:0] in_3,
  output [7:0] out_4
);

  wire and_1_out, and_2_out, and_3_out, and_4_out, and_5_out, and_6_out, and_7_out, and_8_out, and_9_out,
       n8bit_adder_1_out_19, n8bit_adder_1_out_20, n8bit_adder_1_out_21, n8bit_adder_1_out_22,
       n8bit_adder_1_out_23, n8bit_adder_1_out_24, n8bit_adder_1_out_25, n8bit_adder_1_out_26, not_1_out,
       not_2_out, not_3_out, not_4_out, not_5_out, not_6_out, not_7_out, not_8_out, not_9_out, not_10_out;

  not not_1 (not_1_out, in_1);
  and and_1 (and_1_out, not_1_out, in_2);
  not not_2 (not_2_out, and_1_out);
  not not_3 (not_3_out, in_3[0]);
  not not_4 (not_4_out, in_3[1]);
  not not_5 (not_5_out, in_3[2]);
  not not_6 (not_6_out, in_3[3]);
  not not_7 (not_7_out, in_3[4]);
  not not_8 (not_8_out, in_3[5]);
  not not_9 (not_9_out, in_3[6]);
  not not_10 (not_10_out, in_3[7]);
  and and_2 (and_2_out, not_2_out, in_3[0]);
  and and_3 (and_3_out, in_3[1], not_2_out);
  and and_4 (and_4_out, in_3[2], not_2_out);
  and and_5 (and_5_out, in_3[3], not_2_out);
  and and_6 (and_6_out, in_3[4], not_2_out);
  and and_7 (and_7_out, in_3[5], not_2_out);
  and and_8 (and_8_out, in_3[6], not_2_out);
  and and_9 (and_9_out, in_3[7], not_2_out);
  _8bit_adder u_8bit_adder_1 (
    .PLA_input(and_1_out), .in_10(1'b0), .in_11(1'b0), .in_12(1'b0), .in_13(1'b0), .in_14(1'b0),
    .in_15(1'b0), .in_16(1'b0), .in_17(1'b1), .in_2(not_10_out), .in_3(not_9_out), .in_4(not_8_out),
    .in_5(not_7_out), .in_6(not_6_out), .in_7(not_5_out), .in_8(not_4_out), .in_9(not_3_out),
    .out_19(n8bit_adder_1_out_19), .out_20(n8bit_adder_1_out_20), .out_21(n8bit_adder_1_out_21),
    .out_22(n8bit_adder_1_out_22), .out_23(n8bit_adder_1_out_23), .out_24(n8bit_adder_1_out_24),
    .out_25(n8bit_adder_1_out_25), .out_26(n8bit_adder_1_out_26));  // open: out_18, Zero_output_flag
  or or_1 (out_4[6], and_8_out, n8bit_adder_1_out_20);
  or or_2 (out_4[7], n8bit_adder_1_out_19, and_9_out);
  or or_3 (out_4[5], n8bit_adder_1_out_21, and_7_out);
  or or_4 (out_4[4], and_6_out, n8bit_adder_1_out_22);
  or or_5 (out_4[3], n8bit_adder_1_out_23, and_5_out);
  or or_6 (out_4[2], and_4_out, n8bit_adder_1_out_24);
  or or_7 (out_4[1], and_3_out, n8bit_adder_1_out_25);
  or or_8 (out_4[0], and_2_out, n8bit_adder_1_out_26);
endmodule

module A_B_comparator (
  input  [7:0] in_1,
  input  [7:0] in_2,
  output out_3
);

  wire and_1_out, and_2_out, and_3_out, and_4_out, and_5_out, not_1_out, not_2_out, not_3_out, not_4_out,
       xnor_1_out, xnor_2_out, xor_1_out;

  not not_1 (not_1_out, in_1[7]);
  and and_1 (and_1_out, in_2[7], not_1_out);
  xnor xnor_1 (xnor_1_out, in_2[7], in_1[7]);
  not not_2 (not_2_out, in_1[6]);
  and and_2 (and_2_out, in_2[6], not_2_out);
  and and_3 (and_3_out, xnor_1_out, and_2_out);
  xnor xnor_2 (xnor_2_out, in_2[6], in_1[6]);
  not not_3 (not_3_out, in_1[5]);
  and and_4 (and_4_out, xnor_2_out, in_2[5], xnor_1_out, not_3_out);
  or or_1 (out_3, and_1_out, and_3_out, and_4_out, and_5_out);
  not not_4 (not_4_out, in_1[4]);
  xor xor_1 (xor_1_out, in_1[5], in_2[5]);
  and and_5 (and_5_out, xnor_2_out, xnor_1_out, xor_1_out, in_2[4], not_4_out);
endmodule

module A_B_comparator_2 (
  input  [7:0] in_1,
  input  [7:0] in_2,
  output out_3
);

  wire xnor_1_out, xnor_2_out, xnor_3_out, xnor_4_out, xnor_5_out, xnor_6_out, xnor_7_out, xnor_8_out;

  xnor xnor_1 (xnor_1_out, in_2[7], in_1[7]);
  xnor xnor_2 (xnor_2_out, in_2[6], in_1[6]);
  xnor xnor_3 (xnor_3_out, in_2[5], in_1[5]);
  xnor xnor_4 (xnor_4_out, in_2[3], in_1[3]);
  xnor xnor_5 (xnor_5_out, in_2[4], in_1[4]);
  and and_1 (out_3, xnor_1_out, xnor_2_out, xnor_3_out, xnor_5_out, xnor_4_out, xnor_6_out, xnor_7_out, xnor_8_out);
  xnor xnor_6 (xnor_6_out, in_2[2], in_1[2]);
  xnor xnor_7 (xnor_7_out, in_2[1], in_1[1]);
  xnor xnor_8 (xnor_8_out, in_2[0], in_1[0]);
endmodule

module _3bit_async_reg (
  input  [2:0] in_1,
  output [2:0] out_2
);

  D_Flip_Flop #(.trigger("high")) d_ff_1 (.clk(1'b1), .D(in_1[2]), .Q(out_2[2]));  // open: Qn, preset, en, reset
  D_Flip_Flop #(.trigger("high")) d_ff_2 (.clk(1'b1), .D(in_1[1]), .Q(out_2[1]));  // open: Qn, preset, en, reset
  D_Flip_Flop #(.trigger("high")) d_ff_3 (.clk(1'b1), .D(in_1[0]), .Q(out_2[0]));  // open: Qn, preset, en, reset
endmodule

module RomWrite (
  input  [7:0] in_1,
  input  [7:0] in_2,
  input  [7:0] in_3,
  input  [7:0] in_4,
  input  [7:0] in_5,
  input  [7:0] in_6,
  input  [7:0] in_7,
  input  [7:0] in_8,
  input  [7:0] in_9,
  input  [7:0] in_10,
  input  [7:0] in_11,
  input  [7:0] in_12,
  input  [7:0] in_13,
  input  [7:0] in_14,
  input  [7:0] in_15,
  input  [7:0] in_16,
  input  [7:0] in_17,
  input  [7:0] in_18,
  input  [7:0] in_19,
  input  [7:0] in_20,
  input  [7:0] in_21,
  input  [7:0] in_22,
  input  [7:0] in_23,
  input  [7:0] in_24,
  input  [7:0] in_25,
  input  [7:0] in_26,
  input  [7:0] in_27,
  input  [7:0] in_28,
  input  [7:0] in_29,
  input  [7:0] in_30,
  input  [7:0] in_31,
  input  [7:0] in_32,
  input  in_33,
  output [7:0] out_34,
  output [7:0] out_35,
  output [7:0] out_36,
  output [7:0] out_37,
  output [7:0] out_38,
  output [7:0] out_39,
  output [7:0] out_40,
  output [7:0] out_41,
  output [7:0] out_42,
  output [7:0] out_43,
  output [7:0] out_44,
  output [7:0] out_45,
  output [7:0] out_46,
  output [7:0] out_47,
  output [7:0] out_48,
  output [7:0] out_49
);

  Multiplexer #(.width(8), .disabled(0), .enable("false")) multiplexer_1 (
    .in0(in_1), .in1(in_2), .out(out_34), .sel(in_33));
  Multiplexer #(.width(8), .disabled(0), .enable("false")) multiplexer_2 (
    .in0(in_3), .in1(in_4), .out(out_35), .sel(in_33));
  Multiplexer #(.width(8), .disabled(0), .enable("false")) multiplexer_3 (
    .in0(in_5), .in1(in_6), .out(out_36), .sel(in_33));
  Multiplexer #(.width(8), .disabled(0), .enable("false")) multiplexer_4 (
    .in0(in_7), .in1(in_8), .out(out_37), .sel(in_33));
  Multiplexer #(.width(8), .disabled(0), .enable("false")) multiplexer_5 (
    .in0(in_9), .in1(in_10), .out(out_38), .sel(in_33));
  Multiplexer #(.width(8), .disabled(0), .enable("false")) multiplexer_6 (
    .in0(in_11), .in1(in_12), .out(out_39), .sel(in_33));
  Multiplexer #(.width(8), .disabled(0), .enable("false")) multiplexer_7 (
    .in0(in_13), .in1(in_14), .out(out_40), .sel(in_33));
  Multiplexer #(.width(8), .disabled(0), .enable("false")) multiplexer_8 (
    .in0(in_15), .in1(in_16), .out(out_41), .sel(in_33));
  Multiplexer #(.width(8), .disabled(0), .enable("false")) multiplexer_9 (
    .in0(in_17), .in1(in_18), .out(out_42), .sel(in_33));
  Multiplexer #(.width(8), .disabled(0), .enable("false")) multiplexer_10 (
    .in0(in_19), .in1(in_20), .out(out_43), .sel(in_33));
  Multiplexer #(.width(8), .disabled(0), .enable("false")) multiplexer_11 (
    .in0(in_21), .in1(in_22), .out(out_44), .sel(in_33));
  Multiplexer #(.width(8), .disabled(0), .enable("false")) multiplexer_12 (
    .in0(in_23), .in1(in_24), .out(out_45), .sel(in_33));
  Multiplexer #(.width(8), .disabled(0), .enable("false")) multiplexer_13 (
    .in0(in_25), .in1(in_26), .out(out_46), .sel(in_33));
  Multiplexer #(.width(8), .disabled(0), .enable("false")) multiplexer_14 (
    .in0(in_27), .in1(in_28), .out(out_47), .sel(in_33));
  Multiplexer #(.width(8), .disabled(0), .enable("false")) multiplexer_15 (
    .in0(in_29), .in1(in_30), .out(out_48), .sel(in_33));
  Multiplexer #(.width(8), .disabled(0), .enable("false")) multiplexer_16 (
    .in0(in_31), .in1(in_32), .out(out_49), .sel(in_33));
endmodule
